# Fritzing sketch Wiring_Display (saved by Fritzing 0.9.3b)
breadboards: 1

parts:
  LCD2 = LCD screen
  LCM1602_IIC2 = LCM1602 IIC [part_number="LCM1602 IIC" package="DIP (Dual Inline) [THT]"]
  S3 = Pushbutton [part_number="LCD Backlight" package="[THT]"]
  J3 = AVR ISP 6 Pin [package=2x3_lock]

nets:
  VSS: LCD2.VSS, LCM1602_IIC2.VSS
  VDD: LCD2.VDD, LCM1602_IIC2.VDD
  N1: LCD2.V0, LCM1602_IIC2.V0
  N2: LCD2.RS, LCM1602_IIC2.RS
  N3: LCD2.R/W, LCM1602_IIC2.RW
  N4: LCD2.E, LCM1602_IIC2.E
  N5: LCD2.DB0, LCM1602_IIC2.D0
  N6: LCD2.DB1, LCM1602_IIC2.D1
  N7: LCD2.DB2, LCM1602_IIC2.D2
  N8: LCD2.DB3, LCM1602_IIC2.D3
  N9: LCD2.DB4, LCM1602_IIC2.D4
  N10: LCD2.DB5, LCM1602_IIC2.D5
  N11: LCD2.DB6, LCM1602_IIC2.D6
  N12: LCD2.DB7, LCM1602_IIC2.D7
  N13: LCD2.LED+, LCM1602_IIC2.A
  N14: LCD2.LED-, LCM1602_IIC2.K
  N15: LCM1602_IIC2.GND, S3.Pin_1, S3.Pin_2, J3.2
  N16: LCM1602_IIC2.VCC, J3.6
  N17: LCM1602_IIC2.SDA, J3.3
  N18: LCM1602_IIC2.SCL, J3.4
  N19: LCM1602_IIC2.LED_A, LCM1602_IIC2.LED_B
  N20: S3.Pin_3, S3.Pin_4, J3.1

custom parts:
  LCM1602 IIC: I2C-Module to use a 1602 or 2004 LCD on with the wire.h libory Serial LCD Modul
